# Fritzing sketch Squawkers McGraw Wiring (saved by Fritzing 0.9.4)

parts:
  Part1 = Arduino Nano (Rev3.0) (ICSP)
  L298N1 = L298N DC motor driver
  JACK1 = 2.1mm Barrel Jack with Terminal Block
  Part2 = Thumb Joystick
  S1 = Square Pushbutton

nets:
  N1: Part1.D4, L298N1.IN4
  N2: Part1.D5, L298N1.IN3
  N3: Part1.D6, L298N1.IN2
  N4: Part1.D7, L298N1.IN1
  GND: Part1.GND, Part2.GND, S1.leg0
  5V: Part1.5V, Part2.VCC
  N5: Part1.A5, Part2.VERT
  N6: Part1.A4, Part2.HORZ
  N7: Part1.A3, Part2.SEL
  N8: Part1.A2, S1.leg1
  N9: L298N1.12V, JACK1.POS
  N10: L298N1.GND, JACK1.NEG

notes:
  Head Motor
  Body Motor
  Tongue Sensor
  Eyelid Sensors
  Leg Sensor

custom parts:
  L298N DC motor driver: 2x DC motor driver with 78M05 positive voltage regulator (7..35 V) L298N: max 46 V, 2 A Set 5 V Enable jumper to enable 5 V regultor (needed for the L298N) and +5 V output at screw terminal or supply external +5 V at screw terminal Set ENA and/or ENB to +5 V to enable motor permanently or supply ENA and/or ENB with PWM signal IN1 and IN2 set rotation directory for motor A (OUT1/OUT2) IN2 and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
